# Fritzing sketch finger (saved by Fritzing 0.9.3b)
breadboards: 1

parts:
  Part1 = sensor_biometrico
  Part2 = Arduino Mega 2560 (Rev3)
  Part3 = Arduino Ethernet Shield (Rev3)

nets:
  VCC: Part1.VCC, Part3.5V
  N1: Part1.TX, Part2.A8
  N2: Part1.RX, Part2.A9
  GND: Part1.GND, Part3.GND

custom parts:
  sensor_biometrico: Adafruit Optical Fingerprint Sensor
