# Fritzing sketch leds (saved by Fritzing 0.9.3b)
breadboards: 1

parts:
  Part1 = Arduino Mega 2560 (Rev3)
  Part2 = Arduino Ethernet Shield (Rev3)
  R1 = Resistor [tolerance=±5% resistance=220 package=THT]
  LED1 = LED - 5mm [color="Red (633nm)" package="5 mm [THT]"]
  LED2 = LED - 5mm [color="Red (633nm)" package="5 mm [THT]"]
  R2 = Resistor [tolerance=±5% resistance=220 package=THT]
  J1 = Piezo Speaker

nets:
  N1: Part1.D34, J1.pin1
  N2: Part2.PWM_D6, R2.Pin_0
  N3: Part2.D7, R1.Pin_1
  N4: Part2.GND, LED1.anode, LED2.anode, J1.pin2
  N5: R1.Pin_0, LED2.cathode
  N6: LED1.cathode, R2.Pin_1
