# Fritzing sketch rfid (saved by Fritzing 0.9.3b)
circuit board: 8.46667cm x 5.64444cm
breadboards: 1

parts:
  Componente1 = RFID-RC522-v2
  Componente2 = Arduino Mega 2560 (Rev3)
  Part1 = Arduino Ethernet Shield (Rev3)

nets:
  N1: Componente1.SDA, Componente2.D53
  N2: Componente1.SCK, Componente2.D52
  N3: Componente1.MOSI, Componente2.D51
  N4: Componente1.MISO, Componente2.D50
  GND: Componente1.GND, Part1.GND
  N5: Componente1.RST, Componente2.D49
  3.3V: Componente1.3.3V, Part1.3V3

custom parts:
  RFID-RC522-v2: A simple China made RFID-RC522 Reader; do check the pin labels, as this is a MFRC522 based clone.

// code stored in the sketch: Untitled2.ino
/*
 * 
 * All the resources for this project: http://randomnerdtutorials.com/
 * Modified by José Vicente
 * 
 * Created by Japtech
 * 
 */
 
#include <SPI.h>
#include <MFRC522.h>
#include <LiquidCrystal.h>
 
#define SS_PIN 53
#define RST_PIN 6
LiquidCrystal lcd(12, 11, 5, 4, 3, 2);

MFRC522 mfrc522(SS_PIN, RST_PIN);   // Create MFRC522 instance.

void setup() 
{
  lcd.begin(16, 2);
  pinMode(7, OUTPUT);
  pinMode(8, OUTPUT);
  Serial.begin(9600);   // Initiate a serial communication
  SPI.begin();      // Initiate  SPI bus
  mfrc522.PCD_Init();   // Initiate MFRC522
  Serial.println("Approximate your card to the reader...");
  Serial.println();
  lcd.print("waiting for card");
}
void loop() 
{
  // Look for new cards
  
  if ( ! mfrc522.PICC_IsNewCardPresent()) 
  {
    return;
  }
  // Select one of the cards
  if ( ! mfrc522.PICC_ReadCardSerial()) 
  {
    return;
  }
  //Show UID on serial monitor
  Serial.print("UID tag :");
  String content= "";
  byte letter;
  for (byte i = 0; i < mfrc522.uid.size; i++) 
  {
     Serial.print(mfrc522.uid.uidByte[i] < 0x10 ? " 0" : " ");
     Serial.print(mfrc522.uid.uidByte[i], HEX);
         
     content.concat(String(mfrc522.uid.uidByte[i] < 0x10 ? " 0" : " "));
     content.concat(String(mfrc522.uid.uidByte[i], HEX));
  }
  Serial.println();
  Serial.print("Message : ");
  content.toUpperCase();
  if (content.substring(1) == "63 8C E5 C7") //change here the UID of the card/cards that you want to give access
  {
    Serial.println("Authorized access");
    lcd.clear();
    lcd.print("Authorized access");
    digitalWrite(7, HIGH);
    delay(3000);
    digitalWrite(7, LOW);
    lcd.clear();
    lcd.print("waiting for card");
    Serial.println();
  }
 
 else   {
    Serial.println(" Access denied");
    lcd.clear();
    lcd.print(" Access denied");
    digitalWrite(8, HIGH);
    delay(3000);
    digitalWrite(8, LOW);
    lcd.clear();
    lcd.print("waiting for card");
  }
}
